// Logisim project Logic_proiect.circ as structural Verilog: 1 circuit, main circuit main
module main (
);

  wire and_1_out, and_2_out, and_3_out, and_4_out, and_5_out, button_1_out, button_2_out, clock_1_out,
       j_k_ff_1_q, n7447_1_pin3, n7447_1_pin9, n7447_1_pin10, n7447_1_pin11, n7447_1_pin12, n7447_1_pin13,
       n7447_1_pin14, n7447_1_pin15, n7447_2_pin3, n7447_2_pin9, n7447_2_pin10, n7447_2_pin11, n7447_2_pin12,
       n7447_2_pin13, n7447_2_pin14, n7447_2_pin15, n7447_3_pin3, n7447_3_pin9, n7447_3_pin10, n7447_3_pin11,
       n7447_3_pin12, n7447_3_pin13, n7447_3_pin14, n7447_3_pin15, n7447_4_pin3, n7447_4_pin9, n7447_4_pin10,
       n7447_4_pin11, n7447_4_pin12, n7447_4_pin13, n7447_4_pin14, n7447_4_pin15, not_1_out, not_2_out,
       not_3_out, not_4_out, or_1_out, or_2_out, or_3_out, or_4_out;
  wire [3:0] counter_1_q, counter_2_q, counter_3_q, counter_4_q;

  Button button_1 (.out(button_1_out));
  J_K_Flip_Flop j_k_ff_1 (.J(1'b1), .K(1'b1), .clk(button_1_out), .Q(j_k_ff_1_q));  // open: Qn, preset, reset
  Clock clock_1 (.out(clock_1_out));
  and and_1 (and_1_out, j_k_ff_1_q, clock_1_out);
  Button button_2 (.out(button_2_out));
  Pull_Resistor pull_resistor_1 (.node(button_2_out));
  or or_1 (or_1_out, button_2_out, and_2_out);
  or or_2 (or_2_out, button_2_out, and_3_out);
  or or_3 (or_3_out, button_2_out, and_4_out);
  or or_4 (or_4_out, button_2_out, and_5_out);
  Counter #(.max('hf), .width(4)) counter_1 (
    .clr(or_1_out), .load(not_1_out), .up(1'b1), .count(and_3_out), .clk(and_3_out), .Q(counter_1_q));  // open: D, carry
  not not_1 (not_1_out, 1'b1);
  Counter #(.max('hf), .width(4)) counter_2 (
    .clr(or_2_out), .load(not_2_out), .up(1'b1), .count(and_4_out), .clk(and_4_out), .Q(counter_2_q));  // open: D, carry
  not not_2 (not_2_out, 1'b1);
  Counter #(.max('hf), .width(4)) counter_3 (
    .clr(or_3_out), .load(not_3_out), .up(1'b1), .count(and_5_out), .clk(and_5_out), .Q(counter_3_q));  // open: D, carry
  not not_3 (not_3_out, 1'b1);
  Counter #(.max('hf), .width(4)) counter_4 (
    .clr(or_4_out), .load(not_4_out), .up(1'b1), .count(1'b1), .clk(and_1_out), .Q(counter_4_q));  // open: D, carry
  not not_4 (not_4_out, 1'b1);
  and and_2 (and_2_out, counter_1_q[2], counter_1_q[1]);
  and and_3 (and_3_out, counter_2_q[3], counter_2_q[1]);
  and and_4 (and_4_out, counter_3_q[1], counter_3_q[3]);
  and and_5 (and_5_out, counter_4_q[3], counter_4_q[1]);
  _7447 u_7447_1 (
    .pin1(counter_1_q[1]), .pin2(counter_1_q[2]), .pin3(n7447_1_pin3), .pin4(n7447_1_pin3),
    .pin5(n7447_1_pin3), .pin6(counter_1_q[3]), .pin7(counter_1_q[0]), .pin15(n7447_1_pin15),
    .pin14(n7447_1_pin14), .pin13(n7447_1_pin13), .pin12(n7447_1_pin12), .pin11(n7447_1_pin11),
    .pin10(n7447_1_pin10), .pin9(n7447_1_pin9));
  _7447 u_7447_2 (
    .pin1(counter_2_q[1]), .pin2(counter_2_q[2]), .pin3(n7447_2_pin3), .pin4(n7447_2_pin3),
    .pin5(n7447_2_pin3), .pin6(counter_2_q[3]), .pin7(counter_2_q[0]), .pin15(n7447_2_pin15),
    .pin14(n7447_2_pin14), .pin13(n7447_2_pin13), .pin12(n7447_2_pin12), .pin11(n7447_2_pin11),
    .pin10(n7447_2_pin10), .pin9(n7447_2_pin9));
  _7447 u_7447_3 (
    .pin1(counter_3_q[1]), .pin2(counter_3_q[2]), .pin3(n7447_3_pin3), .pin4(n7447_3_pin3),
    .pin5(n7447_3_pin3), .pin6(counter_3_q[3]), .pin7(counter_3_q[0]), .pin15(n7447_3_pin15),
    .pin14(n7447_3_pin14), .pin13(n7447_3_pin13), .pin12(n7447_3_pin12), .pin11(n7447_3_pin11),
    .pin10(n7447_3_pin10), .pin9(n7447_3_pin9));
  _7447 u_7447_4 (
    .pin1(counter_4_q[1]), .pin2(counter_4_q[2]), .pin3(n7447_4_pin3), .pin4(n7447_4_pin3),
    .pin5(n7447_4_pin3), .pin6(counter_4_q[3]), .pin7(counter_4_q[0]), .pin15(n7447_4_pin15),
    .pin14(n7447_4_pin14), .pin13(n7447_4_pin13), .pin12(n7447_4_pin12), .pin11(n7447_4_pin11),
    .pin10(n7447_4_pin10), .pin9(n7447_4_pin9));
  _7_Segment_Display #(.active("false")) u_7_segment_display_1 (
    .g(n7447_1_pin14), .f(n7447_1_pin15), .a(n7447_1_pin13), .b(n7447_1_pin12), .e(n7447_1_pin9),
    .d(n7447_1_pin10), .c(n7447_1_pin11), .dp(1'b1));
  _7_Segment_Display #(.active("false")) u_7_segment_display_2 (
    .g(n7447_2_pin14), .f(n7447_2_pin15), .a(n7447_2_pin13), .b(n7447_2_pin12), .e(n7447_2_pin9),
    .d(n7447_2_pin10), .c(n7447_2_pin11));  // open: dp
  _7_Segment_Display #(.active("false")) u_7_segment_display_3 (
    .g(n7447_3_pin14), .f(n7447_3_pin15), .a(n7447_3_pin13), .b(n7447_3_pin12), .e(n7447_3_pin9),
    .d(n7447_3_pin10), .c(n7447_3_pin11), .dp(1'b1));
  _7_Segment_Display #(.active("false")) u_7_segment_display_4 (
    .g(n7447_4_pin14), .f(n7447_4_pin15), .a(n7447_4_pin13), .b(n7447_4_pin12), .e(n7447_4_pin9),
    .d(n7447_4_pin10), .c(n7447_4_pin11), .dp(1'b1));
  // also tied to VCC on the sheet: {n7447_2_pin3, n7447_4_pin3, n7447_1_pin3, n7447_3_pin3}
endmodule
